// Logisim project P0_L0_CRC.circ as structural Verilog: 2 circuits, main circuit CRC
module CRC (
  input  [7:0] A,
  input  [3:0] B,
  output [10:0] C
);

  wire [2:0] mod2div_4bit_1_remainder, mod2div_4bit_2_remainder, mod2div_4bit_3_remainder,
       mod2div_4bit_4_remainder, mod2div_4bit_5_remainder, mod2div_4bit_6_remainder, mod2div_4bit_7_remainder;

  mod2div_4bit mod2div_4bit_1 (.divisor(B), .dividend(A[7:4]), .remainder(mod2div_4bit_1_remainder));
  mod2div_4bit mod2div_4bit_2 (
    .divisor(B), .dividend({mod2div_4bit_1_remainder, A[3]}), .remainder(mod2div_4bit_2_remainder));
  mod2div_4bit mod2div_4bit_3 (
    .divisor(B), .dividend({mod2div_4bit_2_remainder, A[2]}), .remainder(mod2div_4bit_3_remainder));
  mod2div_4bit mod2div_4bit_4 (
    .divisor(B), .dividend({mod2div_4bit_3_remainder, A[1]}), .remainder(mod2div_4bit_4_remainder));
  mod2div_4bit mod2div_4bit_5 (
    .divisor(B), .dividend({mod2div_4bit_4_remainder, A[0]}), .remainder(mod2div_4bit_5_remainder));
  mod2div_4bit mod2div_4bit_6 (
    .divisor(B), .dividend({mod2div_4bit_5_remainder, 1'b0}), .remainder(mod2div_4bit_6_remainder));
  mod2div_4bit mod2div_4bit_7 (
    .divisor(B), .dividend({mod2div_4bit_6_remainder, 1'b0}), .remainder(mod2div_4bit_7_remainder));
  mod2div_4bit mod2div_4bit_8 (.divisor(B), .dividend({mod2div_4bit_7_remainder, 1'b0}), .remainder(C[2:0]));

  assign C[10:3] = A;

  // Other names for the same wires on the sheet: CheckCode[2:0] = C[2:0]; _3 = A[0]; Data[7:0] = A; _4 = A[1];
  //   _5 = A[2]; _6 = A[3]; divisor[3:0] = B
endmodule

module mod2div_4bit (
  input  [3:0] divisor,
  input  [3:0] dividend,
  output [2:0] remainder
);

  wire [3:0] multiplexer_1_out;
  wire [3:3] xor_1_out;

  Multiplexer #(.width(4)) multiplexer_1 (
    .in0(4'b0000), .in1(divisor), .out(multiplexer_1_out), .sel(dividend[3]));  // open: en
  assign {xor_1_out[3], remainder} = multiplexer_1_out ^ dividend;  // XOR_Gate xor_1, 4 bits wide
endmodule
