// Logisim project P0_L0_FSM.circ as structural Verilog: 3 circuits, main circuit fsm
module fsm (
  input  CLR,
  input  [1:0] IN,
  output out_3
);

  wire clock_1_out;
  wire [2:0] multiplexer_1_out, register_1_q, state_transition_1_ss0;

  state_transition state_transition_1 (
    .S0(register_1_q[0]), .S1(register_1_q[1]), .S2(register_1_q[2]), .I0(IN[0]), .I1(IN[1]),
    .SS0(state_transition_1_ss0[0]), .SS1(state_transition_1_ss0[1]), .SS2(state_transition_1_ss0[2]));
  Multiplexer #(.width(3)) multiplexer_1 (
    .in0(state_transition_1_ss0), .in1(3'b000), .out(multiplexer_1_out), .sel(CLR));  // open: en
  Register #(.width(3)) register_1 (.D(multiplexer_1_out), .Q(register_1_q), .clk(clock_1_out));  // open: en, clr
  Clock clock_1 (.out(clock_1_out));
  \output  output_1 (
    .S0(register_1_q[0]), .S1(register_1_q[1]), .S2(register_1_q[2]), .I0(IN[0]), .I1(IN[1]), .Z(out_3));

  // Other names for the same wires on the sheet: clr_msg = CLR
endmodule

module state_transition (
  input  S0,
  input  S1,
  input  S2,
  input  I0,
  input  I1,
  output SS0,
  output SS1,
  output SS2
);

  wire and_1_out, and_2_out, and_3_out, and_4_out, and_5_out, and_6_out, and_7_out, and_8_out, and_9_out,
       and_10_out, and_11_out, and_12_out, and_13_out, and_14_out, and_15_out, not_1_out, not_2_out,
       not_3_out, not_4_out, not_5_out, not_6_out, not_7_out, not_8_out, not_9_out, not_10_out, not_11_out,
       not_12_out, not_13_out, not_14_out, not_15_out, not_16_out, not_17_out, not_18_out, not_19_out,
       not_20_out, not_21_out, not_22_out, not_23_out, not_24_out, not_25_out, not_26_out, not_27_out,
       not_28_out, not_29_out, not_30_out, not_31_out, not_32_out, not_33_out, not_34_out, not_35_out,
       not_36_out, not_37_out, not_38_out, not_39_out, not_40_out, not_41_out, not_42_out, not_43_out,
       not_44_out, not_45_out, not_46_out, not_47_out, not_48_out;

  not not_1 (not_1_out, S2);
  not not_2 (not_2_out, S1);
  not not_3 (not_3_out, S0);
  not not_4 (not_4_out, I1);
  not not_5 (not_5_out, S2);
  not not_6 (not_6_out, S0);
  not not_7 (not_7_out, I1);
  not not_8 (not_8_out, S2);
  not not_9 (not_9_out, I1);
  not not_10 (not_10_out, S1);
  not not_11 (not_11_out, S0);
  not not_12 (not_12_out, I1);
  not not_13 (not_13_out, S2);
  not not_14 (not_14_out, S1);
  not not_15 (not_15_out, I1);
  not not_16 (not_16_out, I0);
  not not_17 (not_17_out, S2);
  not not_18 (not_18_out, S1);
  not not_19 (not_19_out, I0);
  not not_20 (not_20_out, S2);
  not not_21 (not_21_out, S0);
  not not_22 (not_22_out, I1);
  not not_23 (not_23_out, I0);
  not not_24 (not_24_out, S2);
  not not_25 (not_25_out, S0);
  not not_26 (not_26_out, I0);
  not not_27 (not_27_out, S2);
  not not_28 (not_28_out, S1);
  not not_29 (not_29_out, I1);
  not not_30 (not_30_out, S2);
  not not_31 (not_31_out, S1);
  not not_32 (not_32_out, I1);
  not not_33 (not_33_out, I0);
  not not_34 (not_34_out, S2);
  not not_35 (not_35_out, S1);
  not not_36 (not_36_out, I0);
  not not_37 (not_37_out, S2);
  not not_38 (not_38_out, S0);
  not not_39 (not_39_out, I1);
  not not_40 (not_40_out, I0);
  not not_41 (not_41_out, S2);
  not not_42 (not_42_out, S0);
  not not_43 (not_43_out, I0);
  not not_44 (not_44_out, S2);
  not not_45 (not_45_out, I1);
  not not_46 (not_46_out, I0);
  not not_47 (not_47_out, S2);
  not not_48 (not_48_out, I0);
  and and_1 (and_1_out, not_1_out, not_2_out, not_3_out, not_4_out, I0);
  and and_2 (and_2_out, not_5_out, S1, not_6_out, not_7_out, I0);
  and and_3 (and_3_out, not_8_out, S1, S0, not_9_out, I0);
  and and_4 (and_4_out, S2, not_10_out, not_11_out, not_12_out, I0);
  and and_5 (and_5_out, not_13_out, not_14_out, S0, not_15_out, not_16_out);
  and and_6 (and_6_out, not_17_out, not_18_out, S0, I1, not_19_out);
  and and_7 (and_7_out, not_20_out, S1, not_21_out, not_22_out, not_23_out);
  and and_8 (and_8_out, not_24_out, S1, not_25_out, I1, not_26_out);
  and and_9 (and_9_out, not_27_out, not_28_out, S0, not_29_out, I0);
  and and_10 (and_10_out, not_30_out, not_31_out, S0, not_32_out, not_33_out);
  and and_11 (and_11_out, not_34_out, not_35_out, S0, I1, not_36_out);
  and and_12 (and_12_out, not_37_out, S1, not_38_out, not_39_out, not_40_out);
  and and_13 (and_13_out, not_41_out, S1, not_42_out, I1, not_43_out);
  and and_14 (and_14_out, not_44_out, S1, S0, not_45_out, not_46_out);
  and and_15 (and_15_out, not_47_out, S1, S0, I1, not_48_out);
  or or_1 (SS0, and_1_out, and_2_out, and_3_out, and_4_out, and_5_out, and_6_out, and_7_out, and_8_out);
  or or_2 (SS1, and_9_out, and_10_out, and_11_out, and_12_out, and_13_out);
  or or_3 (SS2, and_14_out, and_15_out);
endmodule

module \output  (
  input  S0,
  input  S1,
  input  S2,
  input  I0,
  input  I1,
  output Z
);

  wire and_1_out, and_2_out, not_1_out, not_2_out, not_3_out, not_4_out, not_5_out;

  not not_1 (not_1_out, S2);
  not not_2 (not_2_out, I1);
  not not_3 (not_3_out, I0);
  not not_4 (not_4_out, S2);
  not not_5 (not_5_out, I0);
  and and_1 (and_1_out, not_1_out, S1, S0, not_2_out, not_3_out);
  and and_2 (and_2_out, not_4_out, S1, S0, I1, not_5_out);
  or or_1 (Z, and_1_out, and_2_out);
endmodule
