// Logisim project P0_L0_GRF.circ as structural Verilog: 2 circuits, main circuit grf
module grf (
  input  [31:0] WD,
  input  [4:0] A1,
  input  [4:0] A2,
  input  [4:0] A3,
  input  WE,
  input  clk,
  input  rst,
  output [31:0] RD1,
  output [31:0] RD2
);

  wire demultiplexer_2_out1, demultiplexer_2_out2, demultiplexer_2_out3, demultiplexer_2_out4,
       demultiplexer_2_out5, demultiplexer_2_out6, demultiplexer_2_out7, demultiplexer_2_out8,
       demultiplexer_2_out9, demultiplexer_2_out10, demultiplexer_2_out11, demultiplexer_2_out12,
       demultiplexer_2_out13, demultiplexer_2_out14, demultiplexer_2_out15, demultiplexer_2_out16,
       demultiplexer_2_out17, demultiplexer_2_out18, demultiplexer_2_out19, demultiplexer_2_out20,
       demultiplexer_2_out21, demultiplexer_2_out22, demultiplexer_2_out23, demultiplexer_2_out24,
       demultiplexer_2_out25, demultiplexer_2_out26, demultiplexer_2_out27, demultiplexer_2_out28,
       demultiplexer_2_out29, demultiplexer_2_out30, demultiplexer_2_out31, en0, en1, en2, en3, en4, en5,
       en6, en7, en8, en9, en10, en11, en12, en13, en14, en15, en16, en17, en18, en19, en20, en21, en22,
       en23, en24, en25, en26, en27, en28, en29, en30, en31;
  wire [31:0] _0_D, _0_Q, _1_D, _1_Q, _2_D, _2_Q, _3_D, _3_Q, _4_D, _4_Q, _5_D, _5_Q, _6_D, _6_Q, _7_D, _7_Q,
       _8_D, _8_Q, _9_D, _9_Q, _10_D, _10_Q, _11_D, _11_Q, _12_D, _12_Q, _13_D, _13_Q, _14_D, _14_Q, _15_D,
       _15_Q, _16_D, _16_Q, _17_D, _17_Q, _18_D, _18_Q, _19_D, _19_Q, _20_D, _20_Q, _21_D, _21_Q, _22_D,
       _22_Q, _23_D, _23_Q, _24_D, _24_Q, _25_D, _25_Q, _26_D, _26_Q, _27_D, _27_Q, _28_D, _28_Q, _29_D,
       _29_Q, _30_D, _30_Q, _31_D, _31_Q;

  Register #(.width(32)) register_1 (.D(_0_D), .en(en0), .Q(_0_Q), .clk(clk), .clr(rst));
  Register #(.width(32)) register_2 (.D(_8_D), .en(en8), .Q(_8_Q), .clk(clk), .clr(rst));
  Register #(.width(32)) register_3 (.D(_16_D), .en(en16), .Q(_16_Q), .clk(clk), .clr(rst));
  Register #(.width(32)) register_4 (.D(_24_D), .en(en24), .Q(_24_Q), .clk(clk), .clr(rst));
  Register #(.width(32)) register_5 (.D(_1_D), .en(en1), .Q(_1_Q), .clk(clk), .clr(rst));
  Register #(.width(32)) register_6 (.D(_9_D), .en(en9), .Q(_9_Q), .clk(clk), .clr(rst));
  Register #(.width(32)) register_7 (.D(_17_D), .en(en17), .Q(_17_Q), .clk(clk), .clr(rst));
  Register #(.width(32)) register_8 (.D(_25_D), .en(en25), .Q(_25_Q), .clk(clk), .clr(rst));
  Multiplexer #(.select(5), .width(32)) multiplexer_1 (
    .in0(_0_Q), .in1(_1_Q), .in2(_2_Q), .in3(_3_Q), .in4(_4_Q), .in5(_5_Q), .in6(_6_Q), .in7(_7_Q),
    .in8(_8_Q), .in9(_9_Q), .in10(_10_Q), .in11(_11_Q), .in12(_12_Q), .in13(_13_Q), .in14(_14_Q),
    .in15(_15_Q), .in16(_16_Q), .in17(_17_Q), .in18(_18_Q), .in19(_19_Q), .in20(_20_Q), .in21(_21_Q),
    .in22(_22_Q), .in23(_23_Q), .in24(_24_Q), .in25(_25_Q), .in26(_26_Q), .in27(_27_Q), .in28(_28_Q),
    .in29(_29_Q), .in30(_30_Q), .in31(_31_Q), .out(RD1), .sel(A1));  // open: en
  Register #(.width(32)) register_9 (.D(_2_D), .en(en2), .Q(_2_Q), .clk(clk), .clr(rst));
  Register #(.width(32)) register_10 (.D(_10_D), .en(en10), .Q(_10_Q), .clk(clk), .clr(rst));
  Register #(.width(32)) register_11 (.D(_18_D), .en(en18), .Q(_18_Q), .clk(clk), .clr(rst));
  Register #(.width(32)) register_12 (.D(_26_D), .en(en26), .Q(_26_Q), .clk(clk), .clr(rst));
  Multiplexer #(.select(5), .width(32)) multiplexer_2 (
    .in0(_0_Q), .in1(_1_Q), .in2(_2_Q), .in3(_3_Q), .in4(_4_Q), .in5(_5_Q), .in6(_6_Q), .in7(_7_Q),
    .in8(_8_Q), .in9(_9_Q), .in10(_10_Q), .in11(_11_Q), .in12(_12_Q), .in13(_13_Q), .in14(_14_Q),
    .in15(_15_Q), .in16(_16_Q), .in17(_17_Q), .in18(_18_Q), .in19(_19_Q), .in20(_20_Q), .in21(_21_Q),
    .in22(_22_Q), .in23(_23_Q), .in24(_24_Q), .in25(_25_Q), .in26(_26_Q), .in27(_27_Q), .in28(_28_Q),
    .in29(_29_Q), .in30(_30_Q), .in31(_31_Q), .out(RD2), .sel(A2));  // open: en
  Register #(.width(32)) register_13 (.D(_3_D), .en(en3), .Q(_3_Q), .clk(clk), .clr(rst));
  Register #(.width(32)) register_14 (.D(_11_D), .en(en11), .Q(_11_Q), .clk(clk), .clr(rst));
  Register #(.width(32)) register_15 (.D(_19_D), .en(en19), .Q(_19_Q), .clk(clk), .clr(rst));
  Register #(.width(32)) register_16 (.D(_27_D), .en(en27), .Q(_27_Q), .clk(clk), .clr(rst));
  Register #(.width(32)) register_17 (.D(_4_D), .en(en4), .Q(_4_Q), .clk(clk), .clr(rst));
  Register #(.width(32)) register_18 (.D(_12_D), .en(en12), .Q(_12_Q), .clk(clk), .clr(rst));
  Register #(.width(32)) register_19 (.D(_20_D), .en(en20), .Q(_20_Q), .clk(clk), .clr(rst));
  Register #(.width(32)) register_20 (.D(_28_D), .en(en28), .Q(_28_Q), .clk(clk), .clr(rst));
  Demultiplexer #(.select(5), .width(32)) demultiplexer_1 (
    .out0(_0_D), .out1(_1_D), .out2(_2_D), .out3(_3_D), .out4(_4_D), .out5(_5_D), .out6(_6_D), .out7(_7_D),
    .out8(_8_D), .out9(_9_D), .out10(_10_D), .out11(_11_D), .out12(_12_D), .out13(_13_D), .out14(_14_D),
    .out15(_15_D), .out16(_16_D), .out17(_17_D), .out18(_18_D), .out19(_19_D), .out20(_20_D), .out21(_21_D),
    .out22(_22_D), .out23(_23_D), .out24(_24_D), .out25(_25_D), .out26(_26_D), .out27(_27_D), .out28(_28_D),
    .out29(_29_D), .out30(_30_D), .out31(_31_D), .in(WD), .sel(A3));  // open: en
  Register #(.width(32)) register_21 (.D(_5_D), .en(en5), .Q(_5_Q), .clk(clk), .clr(rst));
  Register #(.width(32)) register_22 (.D(_13_D), .en(en13), .Q(_13_Q), .clk(clk), .clr(rst));
  Register #(.width(32)) register_23 (.D(_21_D), .en(en21), .Q(_21_Q), .clk(clk), .clr(rst));
  Register #(.width(32)) register_24 (.D(_29_D), .en(en29), .Q(_29_Q), .clk(clk), .clr(rst));
  Register #(.width(32)) register_25 (.D(_6_D), .en(en6), .Q(_6_Q), .clk(clk), .clr(rst));
  Register #(.width(32)) register_26 (.D(_14_D), .en(en14), .Q(_14_Q), .clk(clk), .clr(rst));
  Register #(.width(32)) register_27 (.D(_22_D), .en(en22), .Q(_22_Q), .clk(clk), .clr(rst));
  Register #(.width(32)) register_28 (.D(_30_D), .en(en30), .Q(_30_Q), .clk(clk), .clr(rst));
  Demultiplexer #(.select(5)) demultiplexer_2 (
    .out1(demultiplexer_2_out1), .out2(demultiplexer_2_out2), .out3(demultiplexer_2_out3),
    .out4(demultiplexer_2_out4), .out5(demultiplexer_2_out5), .out6(demultiplexer_2_out6),
    .out7(demultiplexer_2_out7), .out8(demultiplexer_2_out8), .out9(demultiplexer_2_out9),
    .out10(demultiplexer_2_out10), .out11(demultiplexer_2_out11), .out12(demultiplexer_2_out12),
    .out13(demultiplexer_2_out13), .out14(demultiplexer_2_out14), .out15(demultiplexer_2_out15),
    .out16(demultiplexer_2_out16), .out17(demultiplexer_2_out17), .out18(demultiplexer_2_out18),
    .out19(demultiplexer_2_out19), .out20(demultiplexer_2_out20), .out21(demultiplexer_2_out21),
    .out22(demultiplexer_2_out22), .out23(demultiplexer_2_out23), .out24(demultiplexer_2_out24),
    .out25(demultiplexer_2_out25), .out26(demultiplexer_2_out26), .out27(demultiplexer_2_out27),
    .out28(demultiplexer_2_out28), .out29(demultiplexer_2_out29), .out30(demultiplexer_2_out30),
    .out31(demultiplexer_2_out31), .in(1'b1), .sel(A3));  // open: out0, en
  Register #(.width(32)) register_29 (.D(_7_D), .en(en7), .Q(_7_Q), .clk(clk), .clr(rst));
  Register #(.width(32)) register_30 (.D(_15_D), .en(en15), .Q(_15_Q), .clk(clk), .clr(rst));
  Register #(.width(32)) register_31 (.D(_23_D), .en(en23), .Q(_23_Q), .clk(clk), .clr(rst));
  Register #(.width(32)) register_32 (.D(_31_D), .en(en31), .Q(_31_Q), .clk(clk), .clr(rst));
  enable enable_1 (
    .in_1(demultiplexer_2_out1), .in_2(demultiplexer_2_out2), .in_3(demultiplexer_2_out3),
    .in_4(demultiplexer_2_out4), .in_5(demultiplexer_2_out5), .in_6(demultiplexer_2_out6),
    .in_7(demultiplexer_2_out7), .in_8(demultiplexer_2_out8), .in_9(demultiplexer_2_out9),
    .in_10(demultiplexer_2_out10), .in_11(demultiplexer_2_out11), .in_12(demultiplexer_2_out12),
    .in_13(demultiplexer_2_out13), .in_14(demultiplexer_2_out14), .in_15(demultiplexer_2_out15),
    .in_16(demultiplexer_2_out16), .in_17(demultiplexer_2_out17), .in_18(demultiplexer_2_out18),
    .in_19(demultiplexer_2_out19), .in_20(demultiplexer_2_out20), .in_21(demultiplexer_2_out21),
    .in_22(demultiplexer_2_out22), .in_23(demultiplexer_2_out23), .in_24(demultiplexer_2_out24),
    .in_25(demultiplexer_2_out25), .in_26(demultiplexer_2_out26), .in_27(demultiplexer_2_out27),
    .in_28(demultiplexer_2_out28), .in_29(demultiplexer_2_out29), .in_30(demultiplexer_2_out30),
    .in_31(demultiplexer_2_out31), .out_33(en0), .out_34(en1), .out_35(en2), .out_36(en3), .out_37(en4),
    .out_38(en5), .out_39(en6), .out_40(en7), .out_41(en8), .out_42(en9), .out_43(en10), .out_44(en11),
    .out_45(en12), .out_46(en13), .out_47(en14), .out_48(en15), .out_49(en16), .out_50(en17), .out_51(en18),
    .out_52(en19), .out_53(en20), .out_54(en21), .out_55(en22), .out_56(en23), .out_57(en24), .out_58(en25),
    .out_59(en26), .out_60(en27), .out_61(en28), .out_62(en29), .out_63(en30), .out_64(en31), .in_32(WE));
endmodule

module enable (
  input  in_1,
  input  in_2,
  input  in_3,
  input  in_4,
  input  in_5,
  input  in_6,
  input  in_7,
  input  in_8,
  input  in_9,
  input  in_10,
  input  in_11,
  input  in_12,
  input  in_13,
  input  in_14,
  input  in_15,
  input  in_16,
  input  in_17,
  input  in_18,
  input  in_19,
  input  in_20,
  input  in_21,
  input  in_22,
  input  in_23,
  input  in_24,
  input  in_25,
  input  in_26,
  input  in_27,
  input  in_28,
  input  in_29,
  input  in_30,
  input  in_31,
  input  in_32,
  output out_33,
  output out_34,
  output out_35,
  output out_36,
  output out_37,
  output out_38,
  output out_39,
  output out_40,
  output out_41,
  output out_42,
  output out_43,
  output out_44,
  output out_45,
  output out_46,
  output out_47,
  output out_48,
  output out_49,
  output out_50,
  output out_51,
  output out_52,
  output out_53,
  output out_54,
  output out_55,
  output out_56,
  output out_57,
  output out_58,
  output out_59,
  output out_60,
  output out_61,
  output out_62,
  output out_63,
  output out_64
);

  and and_1 (out_33, 1'b0, in_32);
  and and_2 (out_34, in_1, in_32);
  and and_3 (out_35, in_2, in_32);
  and and_4 (out_36, in_3, in_32);
  and and_5 (out_37, in_4, in_32);
  and and_6 (out_38, in_5, in_32);
  and and_7 (out_39, in_6, in_32);
  and and_8 (out_40, in_7, in_32);
  and and_9 (out_41, in_8, in_32);
  and and_10 (out_42, in_9, in_32);
  and and_11 (out_43, in_10, in_32);
  and and_12 (out_44, in_11, in_32);
  and and_13 (out_45, in_12, in_32);
  and and_14 (out_46, in_13, in_32);
  and and_15 (out_47, in_14, in_32);
  and and_16 (out_48, in_15, in_32);
  and and_17 (out_49, in_16, in_32);
  and and_18 (out_50, in_17, in_32);
  and and_19 (out_51, in_18, in_32);
  and and_20 (out_52, in_19, in_32);
  and and_21 (out_53, in_20, in_32);
  and and_22 (out_54, in_21, in_32);
  and and_23 (out_55, in_22, in_32);
  and and_24 (out_56, in_23, in_32);
  and and_25 (out_57, in_24, in_32);
  and and_26 (out_58, in_25, in_32);
  and and_27 (out_59, in_26, in_32);
  and and_28 (out_60, in_27, in_32);
  and and_29 (out_61, in_28, in_32);
  and and_30 (out_62, in_29, in_32);
  and and_31 (out_63, in_30, in_32);
  and and_32 (out_64, in_31, in_32);
endmodule
