// Logisim project P0_L1_ftoi.circ as structural Verilog: 3 circuits, main circuit ftoi
module ftoi (
  input  [15:0] float,
  output [31:0] \int 
);

  wire comparator_1_lt, comparator_2_eq, or_1_out;
  wire [4:0] subtractor_1_out;
  wire [31:0] multiplexer_1_out, shift_get_1_out_3;

  Subtractor #(.width(5)) subtractor_1 (.a(float[14:10]), .b(5'b01111), .out(subtractor_1_out));  // open: bin, bout
  Comparator #(.width(5), .mode("unsigned")) comparator_1 (
    .a(float[14:10]), .b(5'b01111), .lt(comparator_1_lt));  // open: gt, eq
  Comparator #(.width(5), .mode("unsigned")) comparator_2 (
    .a(float[14:10]), .b({5{1'b1}}), .eq(comparator_2_eq));  // open: gt, lt
  shift_get shift_get_1 (.tar(float[9:0]), .shift_bit(subtractor_1_out), .out_3(shift_get_1_out_3));
  or or_1 (or_1_out, comparator_1_lt, comparator_2_eq);
  Multiplexer #(.width(32)) multiplexer_1 (
    .in0(shift_get_1_out_3), .in1({32{1'b0}}), .out(multiplexer_1_out), .sel(or_1_out));  // open: en
  utos utos_1 (.\unsigned (multiplexer_1_out), .\signed (\int ), .sgn(float[15]));

  // Other names for the same wires on the sheet: frac[9:0] = float[9:0]; exp[4:0] = float[14:10]; sgn = float[15]
endmodule

module utos (
  input  [31:0] \unsigned ,
  input  sgn,
  output [31:0] \signed 
);

  wire [31:0] adder_1_out, not_1_out;

  assign not_1_out = ~\unsigned ;  // NOT_Gate not_1, 32 bits wide
  Adder #(.width(32)) adder_1 (.a(not_1_out), .b(32'h1), .out(adder_1_out));  // open: cin, cout
  Multiplexer #(.width(32)) multiplexer_1 (.in0(\unsigned ), .in1(adder_1_out), .out(\signed ), .sel(sgn));  // open: en
endmodule

module shift_get (
  input  [9:0] tar,
  input  [4:0] shift_bit,
  output [31:0] out_3
);

  wire [4:0] subtractor_1_out;

  Subtractor #(.width(5)) subtractor_1 (.a({5{1'b1}}), .b(shift_bit), .out(subtractor_1_out));  // open: bin, bout
  // Probe on subtractor_1_out
  Shifter #(.width(32), .shift("lr")) shifter_1 (.in({1'b1, tar, {21{1'b0}}}), .\dist (subtractor_1_out), .out(out_3));
endmodule
