// Logisim project P0_L1_navigation_2020.circ as structural Verilog: 2 circuits, main circuit navigation
module navigation (
  input  [1:0] dir,
  input  clk,
  input  rst,
  output arrive,
  output hit
);

  wire state_shift_1_h;
  wire [2:0] register_1_q;
  wire [3:0] state_shift_1_ss0;

  state_shift state_shift_1 (
    .S3(arrive), .S2(register_1_q[2]), .S1(register_1_q[1]), .S0(register_1_q[0]), .I1(dir[1]), .I0(dir[0]),
    .SS3(state_shift_1_ss0[3]), .SS2(state_shift_1_ss0[2]), .SS1(state_shift_1_ss0[1]),
    .SS0(state_shift_1_ss0[0]), .H(state_shift_1_h));
  Register #(.width(4)) register_1 (
    .D(state_shift_1_ss0), .Q({arrive, register_1_q}), .clk(clk), .clr(rst));  // open: en
  Register #(.width(1)) register_2 (.D(state_shift_1_h), .Q(hit), .clk(clk), .clr(rst));  // open: en
endmodule

module state_shift (
  input  S3,
  input  S2,
  input  S1,
  input  S0,
  input  I1,
  input  I0,
  output SS3,
  output SS2,
  output SS1,
  output SS0,
  output H
);

  wire and_1_out, and_2_out, and_3_out, and_4_out, and_5_out, and_6_out, and_7_out, and_8_out, and_9_out,
       and_10_out, and_11_out, and_12_out, and_13_out, and_14_out, and_15_out, and_16_out, not_1_out,
       not_2_out, not_3_out, not_4_out, not_5_out, not_6_out, not_7_out, not_8_out, not_9_out, not_10_out,
       not_11_out, not_12_out, not_13_out, not_14_out, not_15_out, not_16_out, not_17_out, not_18_out,
       not_19_out, not_20_out, not_21_out, not_22_out, not_23_out, not_24_out, not_25_out, not_26_out,
       not_27_out, not_28_out, not_29_out, not_30_out, not_31_out, not_32_out, not_33_out, not_34_out,
       not_35_out, not_36_out, not_37_out, not_38_out, not_39_out, not_40_out, not_41_out, not_42_out,
       not_43_out, not_44_out, not_45_out, not_46_out, not_47_out, not_48_out, not_49_out, not_50_out,
       not_51_out, not_52_out, not_53_out, not_54_out, not_55_out, not_56_out, not_57_out, not_58_out,
       not_59_out, not_60_out, not_61_out, not_62_out, not_63_out, or_1_out, xnor_1_out, xor_1_out;

  not not_1 (not_1_out, S3);
  not not_2 (not_2_out, S2);
  not not_3 (not_3_out, S0);
  not not_4 (not_4_out, I1);
  not not_5 (not_5_out, S3);
  not not_6 (not_6_out, S1);
  not not_7 (not_7_out, S0);
  not not_8 (not_8_out, I1);
  not not_9 (not_9_out, I0);
  not not_10 (not_10_out, S3);
  not not_11 (not_11_out, S2);
  not not_12 (not_12_out, S1);
  not not_13 (not_13_out, I1);
  not not_14 (not_14_out, S3);
  not not_15 (not_15_out, S1);
  not not_16 (not_16_out, S0);
  not not_17 (not_17_out, I1);
  not not_18 (not_18_out, S3);
  not not_19 (not_19_out, S1);
  not not_20 (not_20_out, S0);
  not not_21 (not_21_out, I0);
  not not_22 (not_22_out, S3);
  not not_23 (not_23_out, S2);
  not not_24 (not_24_out, S1);
  not not_25 (not_25_out, I1);
  not not_26 (not_26_out, I0);
  not not_27 (not_27_out, S3);
  not not_28 (not_28_out, S2);
  not not_29 (not_29_out, S0);
  not not_30 (not_30_out, I1);
  not not_31 (not_31_out, I0);
  not not_32 (not_32_out, S3);
  not not_33 (not_33_out, S2);
  not not_34 (not_34_out, S0);
  not not_35 (not_35_out, S3);
  not not_36 (not_36_out, S2);
  not not_37 (not_37_out, S1);
  not not_38 (not_38_out, S0);
  not not_39 (not_39_out, I1);
  not not_40 (not_40_out, I0);
  not not_41 (not_41_out, S3);
  not not_42 (not_42_out, S2);
  not not_43 (not_43_out, S0);
  not not_44 (not_44_out, I0);
  not not_45 (not_45_out, S3);
  not not_46 (not_46_out, S1);
  not not_47 (not_47_out, S0);
  not not_48 (not_48_out, S3);
  not not_49 (not_49_out, S2);
  not not_50 (not_50_out, S1);
  not not_51 (not_51_out, S3);
  not not_52 (not_52_out, S2);
  not not_53 (not_53_out, S1);
  not not_54 (not_54_out, S3);
  not not_55 (not_55_out, S2);
  not not_56 (not_56_out, S0);
  xnor xnor_1 (xnor_1_out, I0, I1);
  and and_1 (and_1_out, not_1_out, not_2_out, S1, not_3_out, not_4_out, I0);
  and and_2 (and_2_out, not_5_out, S2, not_6_out, not_7_out, not_8_out, not_9_out);
  and and_3 (and_3_out, not_10_out, not_11_out, not_12_out, S0, not_13_out, I0);
  and and_4 (and_4_out, not_14_out, S2, not_15_out, not_16_out, not_17_out, I0);
  and and_5 (and_5_out, not_18_out, S2, not_19_out, not_20_out, I1, not_21_out);
  and and_6 (and_6_out, not_22_out, not_23_out, not_24_out, S0, not_25_out, not_26_out);
  and and_7 (and_7_out, not_27_out, not_28_out, S1, not_29_out, not_30_out, not_31_out);
  and and_8 (and_8_out, not_32_out, not_33_out, S1, not_34_out, I1, I0);
  and and_9 (and_9_out, not_35_out, not_36_out, not_37_out, not_38_out, not_39_out, not_40_out);
  and and_10 (and_10_out, not_41_out, not_42_out, S1, not_43_out, I1, not_44_out);
  and and_11 (and_11_out, not_45_out, S2, not_46_out, not_47_out, I1, I0);
  and and_12 (and_12_out, not_48_out, not_49_out, not_50_out, S0, I1, I0);
  not not_57 (not_57_out, S3);
  not not_58 (not_58_out, S2);
  not not_59 (not_59_out, S1);
  not not_60 (not_60_out, S0);
  or or_1 (or_1_out, I1, I0);
  not not_61 (not_61_out, S3);
  not not_62 (not_62_out, S1);
  not not_63 (not_63_out, S0);
  xor xor_1 (xor_1_out, I1, I0);
  or or_2 (SS3, and_1_out, and_2_out);
  or or_3 (SS2, and_3_out, and_4_out, and_5_out);
  or or_4 (SS1, and_6_out, and_7_out, and_8_out);
  or or_5 (SS0, and_9_out, and_10_out, and_11_out, and_12_out);
  and and_13 (and_13_out, not_57_out, not_58_out, not_59_out, not_60_out, or_1_out);
  and and_14 (and_14_out, not_51_out, not_52_out, not_53_out, S0, I1, I0);
  and and_15 (and_15_out, not_54_out, not_55_out, S1, not_56_out, xnor_1_out);
  and and_16 (and_16_out, not_61_out, S2, not_62_out, not_63_out, xor_1_out);
  or or_6 (H, and_13_out, and_14_out, and_15_out, and_16_out);
endmodule
