// Logisim project test1.circ as structural Verilog: 1 circuit, main circuit main
module main (
  input  [1:0] s,
  input  [1:0] t0,
  input  [1:0] t1,
  input  [1:0] t2,
  output res
);

  wire comparator_1_gt, decoder_1_out1, decoder_2_out1, decoder_2_out3, decoder_3_out1, decoder_3_out3,
       decoder_4_out1, decoder_4_out3, not_1_out, veto;
  wire [2:0] bitadder_1_out, bitadder_2_out;
  wire [3:0] decoder_1_out0, or_1_out;

  Decoder #(.select(2), .enable("false")) decoder_1 (
    .out0(decoder_1_out0[0]), .out1(decoder_1_out1), .out3(veto), .sel(s));  // open: out2
  Decoder #(.select(2), .enable("false")) decoder_2 (
    .out0(decoder_1_out0[1]), .out1(decoder_2_out1), .out3(decoder_2_out3), .sel(t0));  // open: out2
  Decoder #(.select(2), .enable("false")) decoder_3 (
    .out0(decoder_1_out0[2]), .out1(decoder_3_out1), .out3(decoder_3_out3), .sel(t1));  // open: out2
  Decoder #(.select(2), .enable("false")) decoder_4 (
    .out0(decoder_1_out0[3]), .out1(decoder_4_out1), .out3(decoder_4_out3), .sel(t2));  // open: out2
  or or_1 (or_1_out[0], decoder_1_out1, veto);
  or or_2 (or_1_out[1], decoder_2_out1, decoder_2_out3);
  or or_3 (or_1_out[2], decoder_3_out1, decoder_3_out3);
  or or_4 (or_1_out[3], decoder_4_out1, decoder_4_out3);
  BitAdder #(.width(4)) bitadder_1 (.in0(decoder_1_out0), .out(bitadder_1_out));
  BitAdder #(.width(4)) bitadder_2 (.in0(or_1_out), .out(bitadder_2_out));
  Comparator #(.width(3), .mode("unsigned")) comparator_1 (
    .a(bitadder_1_out), .b(bitadder_2_out), .gt(comparator_1_gt));  // open: eq, lt
  not not_1 (not_1_out, veto);
  and and_1 (res, comparator_1_gt, not_1_out);

  // Notes on the sheet:
  //   agree_num
  //   object_num
endmodule
