// Logisim project test3.circ as structural Verilog: 3 circuits, main circuit main
module main (
  input  [4:0] N,
  output [31:0] Nth
);

  wire clk, en;
  wire [4:0] counter_1_q;
  wire [31:0] adder_1_out, and_1_out, pre1_q, pre2_q;

  Clock clock_1 (.out(clk));
  Counter #(.width(5), .max('h1f), .ongoal("stay")) counter_1 (
    .Q(counter_1_q), .clk(clk));  // open: load, D, count, carry, clr
  register_init pre2 (.init(32'h1), .D(pre1_q), .Q(pre2_q));  // open: clk, rst, en
  register_init pre1 (.init(32'h1), .D(Nth), .Q(pre1_q));  // open: clk, rst, en
  Comparator #(.width(5), .mode("unsigned")) comparator_1 (.a(N), .b(counter_1_q), .gt(en));  // open: eq, lt
  assign and_1_out = pre2_q & pre1_q;  // AND_Gate and_1, 32 bits wide
  Adder #(.width(32)) adder_1 (.a(and_1_out), .b(Nth), .out(adder_1_out));  // open: cin, cout
  Register #(.width(32)) now (.D(adder_1_out), .Q(Nth));  // open: en, clk, clr

  // Notes on the sheet:
  //   S_{-2}=1
  //   S_{-1}=1
endmodule

module register_init (
  input  [31:0] init,
  input  [31:0] D,
  input  en,
  input  clk,
  input  rst,
  output [31:0] Q
);

  wire counter_1_carry;
  wire [31:0] multiplexer_1_out, register_1_q;

  Multiplexer #(.width(32)) multiplexer_1 (.in0(Q), .in1(D), .out(multiplexer_1_out), .sel(en));  // open: en
  Pull_Resistor #(.pull(1)) pull_resistor_1 (.node(en));
  Register #(.width(32)) register_1 (.D(multiplexer_1_out), .Q(register_1_q), .clk(clk), .clr(rst));  // open: en
  Counter #(.width(1), .max('h1), .ongoal("stay")) counter_1 (
    .carry(counter_1_carry), .clk(clk), .clr(rst));  // open: load, D, count, Q
  Pull_Resistor pull_resistor_2 (.node(init));
  Multiplexer #(.width(32)) multiplexer_2 (.in0(init), .in1(register_1_q), .out(Q), .sel(counter_1_carry));  // open: en
endmodule

module select (
  input  [31:0] tar,
  input  [4:0] N,
  output [31:0] out_3
);

  wire comparator_1_gt, comparator_2_gt;
  wire [31:0] multiplexer_1_out, N_t;

  assign N_t = {{27{1'b0}}, N};  // Bit_Extender bit_extender_1
  Comparator #(.width(32), .mode("unsigned")) comparator_1 (.a(N_t), .b(32'h3), .gt(comparator_1_gt));  // open: eq, lt
  Multiplexer #(.width(32)) multiplexer_1 (
    .in0(32'h1), .in1(tar), .out(multiplexer_1_out), .sel(comparator_1_gt));  // open: en
  Multiplexer #(.width(32)) multiplexer_2 (
    .in0({32{1'b0}}), .in1(multiplexer_1_out), .out(out_3), .sel(comparator_2_gt));  // open: en
  Comparator #(.width(32), .mode("unsigned")) comparator_2 (
    .a(N_t), .b({32{1'b0}}), .gt(comparator_2_gt));  // open: eq, lt

  // Notes on the sheet:
  //   if(N<=3) tar
  //   if(N<=0) tar
endmodule
