// Logisim project P3_L0_CPU_v1.3.circ as structural Verilog: 13 circuits, main circuit main
module main (
  input  Rst,
  output [31:0] Instr,
  output RegWrite,
  output [4:0] RegAddr,
  output [31:0] RegData,
  output MemWrite,
  output [4:0] MemAddr,
  output [31:0] MemData
);

  wire alu_1_zero, Clk, ctrl_1_m3sel;
  wire [1:0] ctrl_1_aluop, ctrl_1_extop, ctrl_1_lsel, ctrl_1_m1sel, ctrl_1_m2sel, ctrl_1_npcop, ctrl_1_ssel;
  wire [4:0] im_export_1_im_d_15_11, im_export_1_im_d_20_16, im_export_1_im_d_25_21;
  wire [5:0] im_export_1_im_d_5_0, im_export_1_im_d_31_26;
  wire [15:0] im_export_1_im_d_15_0;
  wire [25:0] im_export_1_im_d_25_0;
  wire [31:0] alu_1_y, dm_1_rd, ext_1_o, grf_1_rd1, multiplexer_3_out, npc_1_npc, npc_1_pc4, register_1_q;

  Clock clock_1 (.out(Clk));
  register_init register_init_1 ();  // open: init, D, en, clk, rst, Q
  Register #(.width(32)) register_1 (.D(npc_1_npc), .Q(register_1_q), .clk(Clk), .clr(Rst));  // open: en
  NPC npc_1 (
    .PC(register_1_q), .IMM(im_export_1_im_d_25_0), .Zero(alu_1_zero), .RA(grf_1_rd1), .NPCOp(ctrl_1_npcop),
    .PC4(npc_1_pc4), .NPC(npc_1_npc));
  ROM #(.addrWidth(16), .dataWidth(32)) rom_1 (.addr(register_1_q[17:2]), .data(Instr));  // open: sel
  IM_export im_export_1 (
    .IM_D(Instr), .IM_D_31_26(im_export_1_im_d_31_26), .IM_D_25_21(im_export_1_im_d_25_21),
    .IM_D_20_16(im_export_1_im_d_20_16), .IM_D_15_11(im_export_1_im_d_15_11),
    .IM_D_5_0(im_export_1_im_d_5_0), .IM_D_15_0(im_export_1_im_d_15_0), .IM_D_25_0(im_export_1_im_d_25_0));  // open: IM_D_10_6
  Multiplexer #(.select(2), .width(5), .enable("false")) multiplexer_1 (
    .in0(im_export_1_im_d_20_16), .in1(im_export_1_im_d_15_11), .in2({5{1'b1}}), .out(RegAddr),
    .sel(ctrl_1_m1sel));  // open: in3
  CTRL ctrl_1 (
    .op(im_export_1_im_d_31_26), .funct(im_export_1_im_d_5_0), .NPCOp(ctrl_1_npcop), .M1Sel(ctrl_1_m1sel),
    .M2Sel(ctrl_1_m2sel), .RFWr(RegWrite), .EXTOp(ctrl_1_extop), .M3Sel(ctrl_1_m3sel), .ALUOp(ctrl_1_aluop),
    .DMWr(MemWrite), .SSel(ctrl_1_ssel), .LSel(ctrl_1_lsel));
  Multiplexer #(.select(2), .width(32), .enable("false")) multiplexer_2 (
    .in0(npc_1_pc4), .in1(dm_1_rd), .in2({alu_1_y[31:7], MemAddr, alu_1_y[1:0]}), .in3(ext_1_o),
    .out(RegData), .sel(ctrl_1_m2sel));
  EXT ext_1 (.I(im_export_1_im_d_15_0), .EXTOp(ctrl_1_extop), .O(ext_1_o));
  GRF grf_1 (
    .WD(RegData), .A1(im_export_1_im_d_25_21), .A2(im_export_1_im_d_20_16), .A3(RegAddr), .Clk(Clk),
    .Rst(Rst), .RD1(grf_1_rd1), .RD2(MemData), .RFWr(RegWrite));
  Multiplexer #(.width(32), .enable("false")) multiplexer_3 (
    .in0(MemData), .in1(ext_1_o), .out(multiplexer_3_out), .sel(ctrl_1_m3sel));
  ALU alu_1 (
    .A(grf_1_rd1), .B(multiplexer_3_out), .ALUOp(ctrl_1_aluop), .Zero(alu_1_zero),
    .Y({alu_1_y[31:7], MemAddr, alu_1_y[1:0]}));
  DM dm_1 (
    .A({alu_1_y[31:7], MemAddr, alu_1_y[1:0]}), .WD(MemData), .DMWr(MemWrite), .Clk(Clk), .Rst(Rst),
    .RD(dm_1_rd), .LSel(ctrl_1_lsel), .SSel(ctrl_1_ssel));

  // Other names for the same wires on the sheet: DMA[4:0] = MemAddr; DMWD[31:0] = MemData; DMWr = MemWrite;
  //   RFA3[4:0] = RegAddr; RFWD[31:0] = RegData; RFWr = RegWrite

  // Notes on the sheet:
  //   M1
  //   M2
  //   M3
endmodule

module tb (
  output [31:0] Instr,
  output RegWrite,
  output [4:0] RegAddr,
  output [31:0] RegData,
  output halt,
  output MemWrite,
  output [4:0] MemAddr,
  output [31:0] MemData
);

  wire clock_1_out, comparator_1_gt;
  wire [7:0] counter_1_q;

  Clock clock_1 (.out(clock_1_out));
  Counter counter_1 (.Q(counter_1_q), .carry(halt), .clk(clock_1_out));  // open: load, D, count, clr
  Comparator comparator_1 (.a(8'h4), .b(counter_1_q), .gt(comparator_1_gt));  // open: eq, lt
  main main_1 (
    .Rst(comparator_1_gt), .Instr(Instr), .RegWrite(RegWrite), .RegAddr(RegAddr), .RegData(RegData),
    .MemWrite(MemWrite), .MemAddr(MemAddr), .MemData(MemData));
endmodule

module CTRL (
  input  [5:0] op,
  input  [5:0] funct,
  output [1:0] NPCOp,
  output [1:0] M1Sel,
  output [1:0] M2Sel,
  output RFWr,
  output [1:0] EXTOp,
  output M3Sel,
  output [1:0] ALUOp,
  output DMWr,
  output [1:0] SSel,
  output [1:0] LSel
);

  wire addu, beq, j, jal, jr, lb, lh, lui, lw, not_1_out, not_2_out, not_3_out, not_4_out, not_5_out,
       not_6_out, not_7_out, not_8_out, not_9_out, not_10_out, not_11_out, not_12_out, op0, ori, sb, sh,
       subu, sw;

  not not_1 (not_1_out, op[5]);
  not not_2 (not_2_out, op[3]);
  not not_3 (not_3_out, op[4]);
  not not_4 (not_4_out, op[2]);
  not not_5 (not_5_out, op[1]);
  not not_6 (not_6_out, op[0]);
  and _00_0000 (op0, not_1_out, not_3_out, not_2_out, not_4_out, not_5_out, not_6_out);
  and u_ori (ori, not_1_out, not_3_out, op[3], op[2], not_5_out, op[0]);
  and u_lw (lw, op[5], not_3_out, not_2_out, not_4_out, op[1], op[0]);
  and u_sw (sw, op[5], not_3_out, op[3], not_4_out, op[1], op[0]);
  and u_beq (beq, not_1_out, not_3_out, not_2_out, op[2], not_5_out, not_6_out);
  and u_jal (jal, not_1_out, not_3_out, not_2_out, not_4_out, op[1], op[0]);
  and u_lui (lui, not_1_out, not_3_out, op[3], op[2], op[1], op[0]);
  and u_j (j, not_1_out, not_3_out, not_2_out, not_4_out, op[1], not_6_out);
  and u_lh (lh, op[5], not_3_out, not_2_out, not_4_out, not_5_out, op[0]);
  and u_lb (lb, op[5], not_3_out, not_2_out, not_4_out, not_5_out, not_6_out);
  and u_sh (sh, op[5], not_3_out, op[3], not_4_out, not_5_out, op[0]);
  and u_sb (sb, op[5], not_3_out, op[3], not_4_out, not_5_out, not_6_out);
  not not_7 (not_7_out, funct[4]);
  not not_8 (not_8_out, funct[5]);
  not not_9 (not_9_out, funct[3]);
  not not_10 (not_10_out, funct[1]);
  not not_11 (not_11_out, funct[2]);
  not not_12 (not_12_out, funct[0]);
  and u_addu (addu, funct[5], not_7_out, not_9_out, not_11_out, not_10_out, funct[0], op0);
  and u_subu (subu, funct[5], not_7_out, not_9_out, not_11_out, funct[1], funct[0], op0);
  and u_jr (jr, not_8_out, not_7_out, funct[3], not_11_out, not_10_out, not_12_out, op0);
  or or_1 (NPCOp[1], jal, jr, j);
  or or_2 (NPCOp[0], beq, jr);
  buf or_3 (M1Sel[1], jal);  // OR_Gate
  or or_4 (M1Sel[0], addu, subu);
  or or_5 (M2Sel[1], addu, subu, ori, lui);
  or or_6 (M2Sel[0], lw, lui, lh, lb);
  or or_7 (RFWr, addu, subu, ori, lw, jal, lui, lh, lb);
  buf or_8 (EXTOp[1], lui);  // OR_Gate
  or or_9 (EXTOp[0], lw, sw, lh, lb, sh, sb);
  or or_10 (M3Sel, sb, ori, lw, sw, lh, lb, sh);
  buf or_11 (ALUOp[1], ori);  // OR_Gate
  buf or_12 (ALUOp[0], subu);  // OR_Gate
  or or_13 (DMWr, sw, sh, sb);
  buf or_14 (SSel[1], sb);  // OR_Gate
  buf or_15 (SSel[0], sh);  // OR_Gate
  buf or_16 (LSel[1], lb);  // OR_Gate
  buf or_17 (LSel[0], lh);  // OR_Gate

  // Notes on the sheet:
  //   延长线
endmodule

module NPC (
  input  [31:0] PC,
  input  [25:0] IMM,
  input  Zero,
  input  [31:0] RA,
  input  [1:0] NPCOp,
  output [31:0] PC4,
  output [31:0] NPC
);

  wire [31:0] adder_1_out, bit_extender_1_out, multiplexer_1_out;

  assign bit_extender_1_out = {{14{IMM[15]}}, {IMM[15:0], 2'b00}};  // Bit_Extender bit_extender_1
  Adder #(.width(32)) adder_1 (.a(PC4), .b(bit_extender_1_out), .out(adder_1_out));  // open: cin, cout
  Multiplexer #(.width(32), .enable("false")) multiplexer_1 (
    .in0(PC4), .in1(adder_1_out), .out(multiplexer_1_out), .sel(Zero));
  Adder #(.width(32)) adder_2 (.a(PC), .b(32'h4), .out(PC4));  // open: cin, cout
  Multiplexer #(.select(2), .width(32), .enable("false")) multiplexer_2 (
    .in0(PC4), .in1(multiplexer_1_out), .in2({PC[31:28], IMM, 2'b00}), .in3(RA), .out(NPC), .sel(NPCOp));

  // Other names for the same wires on the sheet: PCHigh[3:0] = PC[31:28]
endmodule

module IM_export (
  input  [31:0] IM_D,
  output [5:0] IM_D_31_26,
  output [4:0] IM_D_25_21,
  output [4:0] IM_D_20_16,
  output [4:0] IM_D_15_11,
  output [4:0] IM_D_10_6,
  output [5:0] IM_D_5_0,
  output [15:0] IM_D_15_0,
  output [25:0] IM_D_25_0
);


  assign IM_D_5_0 = IM_D[5:0];
  assign IM_D_10_6 = IM_D[10:6];
  assign IM_D_15_0 = IM_D[15:0];
  assign IM_D_15_11 = IM_D[15:11];
  assign IM_D_20_16 = IM_D[20:16];
  assign IM_D_25_0 = IM_D[25:0];
  assign IM_D_25_21 = IM_D[25:21];
  assign IM_D_31_26 = IM_D[31:26];
endmodule

module GRF (
  input  [31:0] WD,
  input  [4:0] A1,
  input  [4:0] A2,
  input  [4:0] A3,
  input  RFWr,
  input  Clk,
  input  Rst,
  output [31:0] RD1,
  output [31:0] RD2
);

  wire decoder_1_out1, decoder_1_out2, decoder_1_out3, decoder_1_out4, decoder_1_out5, decoder_1_out6,
       decoder_1_out7, decoder_1_out8, decoder_1_out9, decoder_1_out10, decoder_1_out11, decoder_1_out12,
       decoder_1_out13, decoder_1_out14, decoder_1_out15, decoder_1_out16, decoder_1_out17, decoder_1_out18,
       decoder_1_out19, decoder_1_out20, decoder_1_out21, decoder_1_out22, decoder_1_out23, decoder_1_out24,
       decoder_1_out25, decoder_1_out26, decoder_1_out27, decoder_1_out28, decoder_1_out29, decoder_1_out30,
       decoder_1_out31, en1, en2, en3, en4, en5, en6, en7, en8, en9, en10, en11, en12, en13, en14, en15,
       en16, en17, en18, en19, en20, en21, en22, en23, en24, en25, en26, en27, en28, en29, en30, en31;
  wire [31:0] _1_D, _1_Q, _2_D, _2_Q, _3_D, _3_Q, _4_D, _4_Q, _5_D, _5_Q, _6_D, _6_Q, _7_D, _7_Q, _8_D, _8_Q,
       _9_D, _9_Q, _10_D, _10_Q, _11_D, _11_Q, _12_D, _12_Q, _13_D, _13_Q, _14_D, _14_Q, _15_D, _15_Q, _16_D,
       _16_Q, _17_D, _17_Q, _18_D, _18_Q, _19_D, _19_Q, _20_D, _20_Q, _21_D, _21_Q, _22_D, _22_Q, _23_D,
       _23_Q, _24_D, _24_Q, _25_D, _25_Q, _26_D, _26_Q, _27_D, _27_Q, _28_D, _28_Q, _29_D, _29_Q, _30_D,
       _30_Q, _31_D, _31_Q;

  Register #(.width(32)) register_1 (.D(_8_D), .en(en8), .Q(_8_Q), .clk(Clk), .clr(Rst));
  Register #(.width(32)) register_2 (.D(_16_D), .en(en16), .Q(_16_Q), .clk(Clk), .clr(Rst));
  Register #(.width(32)) register_3 (.D(_24_D), .en(en24), .Q(_24_Q), .clk(Clk), .clr(Rst));
  Register #(.width(32)) register_4 (.D(_1_D), .en(en1), .Q(_1_Q), .clk(Clk), .clr(Rst));
  Register #(.width(32)) register_5 (.D(_9_D), .en(en9), .Q(_9_Q), .clk(Clk), .clr(Rst));
  Register #(.width(32)) register_6 (.D(_17_D), .en(en17), .Q(_17_Q), .clk(Clk), .clr(Rst));
  Register #(.width(32)) register_7 (.D(_25_D), .en(en25), .Q(_25_Q), .clk(Clk), .clr(Rst));
  Multiplexer #(.select(5), .width(32)) multiplexer_1 (
    .in0({32{1'b0}}), .in1(_1_Q), .in2(_2_Q), .in3(_3_Q), .in4(_4_Q), .in5(_5_Q), .in6(_6_Q), .in7(_7_Q),
    .in8(_8_Q), .in9(_9_Q), .in10(_10_Q), .in11(_11_Q), .in12(_12_Q), .in13(_13_Q), .in14(_14_Q),
    .in15(_15_Q), .in16(_16_Q), .in17(_17_Q), .in18(_18_Q), .in19(_19_Q), .in20(_20_Q), .in21(_21_Q),
    .in22(_22_Q), .in23(_23_Q), .in24(_24_Q), .in25(_25_Q), .in26(_26_Q), .in27(_27_Q), .in28(_28_Q),
    .in29(_29_Q), .in30(_30_Q), .in31(_31_Q), .out(RD1), .sel(A1));  // open: en
  Register #(.width(32)) register_8 (.D(_2_D), .en(en2), .Q(_2_Q), .clk(Clk), .clr(Rst));
  Register #(.width(32)) register_9 (.D(_10_D), .en(en10), .Q(_10_Q), .clk(Clk), .clr(Rst));
  Register #(.width(32)) register_10 (.D(_18_D), .en(en18), .Q(_18_Q), .clk(Clk), .clr(Rst));
  Register #(.width(32)) register_11 (.D(_26_D), .en(en26), .Q(_26_Q), .clk(Clk), .clr(Rst));
  Multiplexer #(.select(5), .width(32)) multiplexer_2 (
    .in0({32{1'b0}}), .in1(_1_Q), .in2(_2_Q), .in3(_3_Q), .in4(_4_Q), .in5(_5_Q), .in6(_6_Q), .in7(_7_Q),
    .in8(_8_Q), .in9(_9_Q), .in10(_10_Q), .in11(_11_Q), .in12(_12_Q), .in13(_13_Q), .in14(_14_Q),
    .in15(_15_Q), .in16(_16_Q), .in17(_17_Q), .in18(_18_Q), .in19(_19_Q), .in20(_20_Q), .in21(_21_Q),
    .in22(_22_Q), .in23(_23_Q), .in24(_24_Q), .in25(_25_Q), .in26(_26_Q), .in27(_27_Q), .in28(_28_Q),
    .in29(_29_Q), .in30(_30_Q), .in31(_31_Q), .out(RD2), .sel(A2));  // open: en
  Register #(.width(32)) register_12 (.D(_3_D), .en(en3), .Q(_3_Q), .clk(Clk), .clr(Rst));
  Register #(.width(32)) register_13 (.D(_11_D), .en(en11), .Q(_11_Q), .clk(Clk), .clr(Rst));
  Register #(.width(32)) register_14 (.D(_19_D), .en(en19), .Q(_19_Q), .clk(Clk), .clr(Rst));
  Register #(.width(32)) register_15 (.D(_27_D), .en(en27), .Q(_27_Q), .clk(Clk), .clr(Rst));
  Register #(.width(32)) register_16 (.D(_4_D), .en(en4), .Q(_4_Q), .clk(Clk), .clr(Rst));
  Register #(.width(32)) register_17 (.D(_12_D), .en(en12), .Q(_12_Q), .clk(Clk), .clr(Rst));
  Register #(.width(32)) register_18 (.D(_20_D), .en(en20), .Q(_20_Q), .clk(Clk), .clr(Rst));
  Register #(.width(32)) register_19 (.D(_28_D), .en(en28), .Q(_28_Q), .clk(Clk), .clr(Rst));
  Demultiplexer #(.select(5), .width(32), .tristate("true")) demultiplexer_1 (
    .out1(_1_D), .out2(_2_D), .out3(_3_D), .out4(_4_D), .out5(_5_D), .out6(_6_D), .out7(_7_D), .out8(_8_D),
    .out9(_9_D), .out10(_10_D), .out11(_11_D), .out12(_12_D), .out13(_13_D), .out14(_14_D), .out15(_15_D),
    .out16(_16_D), .out17(_17_D), .out18(_18_D), .out19(_19_D), .out20(_20_D), .out21(_21_D), .out22(_22_D),
    .out23(_23_D), .out24(_24_D), .out25(_25_D), .out26(_26_D), .out27(_27_D), .out28(_28_D), .out29(_29_D),
    .out30(_30_D), .out31(_31_D), .in(WD), .sel(A3));  // open: out0, en
  Register #(.width(32)) register_20 (.D(_5_D), .en(en5), .Q(_5_Q), .clk(Clk), .clr(Rst));
  Register #(.width(32)) register_21 (.D(_13_D), .en(en13), .Q(_13_Q), .clk(Clk), .clr(Rst));
  Register #(.width(32)) register_22 (.D(_21_D), .en(en21), .Q(_21_Q), .clk(Clk), .clr(Rst));
  Register #(.width(32)) register_23 (.D(_29_D), .en(en29), .Q(_29_Q), .clk(Clk), .clr(Rst));
  Register #(.width(32)) register_24 (.D(_6_D), .en(en6), .Q(_6_Q), .clk(Clk), .clr(Rst));
  Register #(.width(32)) register_25 (.D(_14_D), .en(en14), .Q(_14_Q), .clk(Clk), .clr(Rst));
  Register #(.width(32)) register_26 (.D(_22_D), .en(en22), .Q(_22_Q), .clk(Clk), .clr(Rst));
  Register #(.width(32)) register_27 (.D(_30_D), .en(en30), .Q(_30_Q), .clk(Clk), .clr(Rst));
  Decoder #(.select(5)) decoder_1 (
    .out1(decoder_1_out1), .out2(decoder_1_out2), .out3(decoder_1_out3), .out4(decoder_1_out4),
    .out5(decoder_1_out5), .out6(decoder_1_out6), .out7(decoder_1_out7), .out8(decoder_1_out8),
    .out9(decoder_1_out9), .out10(decoder_1_out10), .out11(decoder_1_out11), .out12(decoder_1_out12),
    .out13(decoder_1_out13), .out14(decoder_1_out14), .out15(decoder_1_out15), .out16(decoder_1_out16),
    .out17(decoder_1_out17), .out18(decoder_1_out18), .out19(decoder_1_out19), .out20(decoder_1_out20),
    .out21(decoder_1_out21), .out22(decoder_1_out22), .out23(decoder_1_out23), .out24(decoder_1_out24),
    .out25(decoder_1_out25), .out26(decoder_1_out26), .out27(decoder_1_out27), .out28(decoder_1_out28),
    .out29(decoder_1_out29), .out30(decoder_1_out30), .out31(decoder_1_out31), .sel(A3));  // open: out0, en
  Register #(.width(32)) register_28 (.D(_7_D), .en(en7), .Q(_7_Q), .clk(Clk), .clr(Rst));
  Register #(.width(32)) register_29 (.D(_15_D), .en(en15), .Q(_15_Q), .clk(Clk), .clr(Rst));
  Register #(.width(32)) register_30 (.D(_23_D), .en(en23), .Q(_23_Q), .clk(Clk), .clr(Rst));
  Register #(.width(32)) register_31 (.D(_31_D), .en(en31), .Q(_31_Q), .clk(Clk), .clr(Rst));
  GRF_enable grf_enable_1 (
    ._1(decoder_1_out1), .in_2(decoder_1_out2), .in_3(decoder_1_out3), .in_4(decoder_1_out4),
    .in_5(decoder_1_out5), .in_6(decoder_1_out6), .in_7(decoder_1_out7), .in_8(decoder_1_out8),
    .in_9(decoder_1_out9), .in_10(decoder_1_out10), .in_11(decoder_1_out11), .in_12(decoder_1_out12),
    .in_13(decoder_1_out13), .in_14(decoder_1_out14), .in_15(decoder_1_out15), .in_16(decoder_1_out16),
    .in_17(decoder_1_out17), .in_18(decoder_1_out18), .in_19(decoder_1_out19), .in_20(decoder_1_out20),
    .in_21(decoder_1_out21), .in_22(decoder_1_out22), .in_23(decoder_1_out23), .in_24(decoder_1_out24),
    .in_25(decoder_1_out25), .in_26(decoder_1_out26), .in_27(decoder_1_out27), .in_28(decoder_1_out28),
    .in_29(decoder_1_out29), .in_30(decoder_1_out30), ._31(decoder_1_out31), .out_33(en1), .out_34(en2),
    .out_35(en3), .out_36(en4), .out_37(en5), .out_38(en6), .out_39(en7), .out_40(en8), .out_41(en9),
    .out_42(en10), .out_43(en11), .out_44(en12), .out_45(en13), .out_46(en14), .out_47(en15), .out_48(en16),
    .out_49(en17), .out_50(en18), .out_51(en19), .out_52(en20), .out_53(en21), .out_54(en22), .out_55(en23),
    .out_56(en24), .out_57(en25), .out_58(en26), .out_59(en27), .out_60(en28), .out_61(en29), .out_62(en30),
    .out_63(en31), .in_32(RFWr));
endmodule

module GRF_enable (
  input  _1,
  input  in_2,
  input  in_3,
  input  in_4,
  input  in_5,
  input  in_6,
  input  in_7,
  input  in_8,
  input  in_9,
  input  in_10,
  input  in_11,
  input  in_12,
  input  in_13,
  input  in_14,
  input  in_15,
  input  in_16,
  input  in_17,
  input  in_18,
  input  in_19,
  input  in_20,
  input  in_21,
  input  in_22,
  input  in_23,
  input  in_24,
  input  in_25,
  input  in_26,
  input  in_27,
  input  in_28,
  input  in_29,
  input  in_30,
  input  _31,
  input  in_32,
  output out_33,
  output out_34,
  output out_35,
  output out_36,
  output out_37,
  output out_38,
  output out_39,
  output out_40,
  output out_41,
  output out_42,
  output out_43,
  output out_44,
  output out_45,
  output out_46,
  output out_47,
  output out_48,
  output out_49,
  output out_50,
  output out_51,
  output out_52,
  output out_53,
  output out_54,
  output out_55,
  output out_56,
  output out_57,
  output out_58,
  output out_59,
  output out_60,
  output out_61,
  output out_62,
  output out_63
);

  and and_1 (out_33, _1, in_32);
  and and_2 (out_34, in_2, in_32);
  and and_3 (out_35, in_3, in_32);
  and and_4 (out_36, in_4, in_32);
  and and_5 (out_37, in_5, in_32);
  and and_6 (out_38, in_6, in_32);
  and and_7 (out_39, in_7, in_32);
  and and_8 (out_40, in_8, in_32);
  and and_9 (out_41, in_9, in_32);
  and and_10 (out_42, in_10, in_32);
  and and_11 (out_43, in_11, in_32);
  and and_12 (out_44, in_12, in_32);
  and and_13 (out_45, in_13, in_32);
  and and_14 (out_46, in_14, in_32);
  and and_15 (out_47, in_15, in_32);
  and and_16 (out_48, in_16, in_32);
  and and_17 (out_49, in_17, in_32);
  and and_18 (out_50, in_18, in_32);
  and and_19 (out_51, in_19, in_32);
  and and_20 (out_52, in_20, in_32);
  and and_21 (out_53, in_21, in_32);
  and and_22 (out_54, in_22, in_32);
  and and_23 (out_55, in_23, in_32);
  and and_24 (out_56, in_24, in_32);
  and and_25 (out_57, in_25, in_32);
  and and_26 (out_58, in_26, in_32);
  and and_27 (out_59, in_27, in_32);
  and and_28 (out_60, in_28, in_32);
  and and_29 (out_61, in_29, in_32);
  and and_30 (out_62, in_30, in_32);
  and and_31 (out_63, _31, in_32);
endmodule

module EXT (
  input  [15:0] I,
  input  [1:0] EXTOp,
  output [31:0] O
);

  wire [31:0] bit_extender_1_out, bit_extender_2_out;

  assign bit_extender_1_out = {{16{1'b0}}, I};  // Bit_Extender bit_extender_1
  assign bit_extender_2_out = {{16{I[15]}}, I};  // Bit_Extender bit_extender_2
  Multiplexer #(.select(2), .width(32), .enable("false")) multiplexer_1 (
    .in0(bit_extender_1_out), .in1(bit_extender_2_out), .in2({I, {16{1'b0}}}), .out(O), .sel(EXTOp));  // open: in3
endmodule

module ALU (
  input  [31:0] A,
  input  [31:0] B,
  input  [1:0] ALUOp,
  output Zero,
  output [31:0] Y
);

  wire [31:0] adder_1_out, or_1_out, subtractor_1_out;

  Adder #(.width(32)) adder_1 (.a(A), .b(B), .out(adder_1_out));  // open: cin, cout
  Subtractor #(.width(32)) subtractor_1 (.a(A), .b(B), .out(subtractor_1_out));  // open: bin, bout
  assign or_1_out = A | B;  // OR_Gate or_1, 32 bits wide
  Comparator #(.width(32)) comparator_1 (.a({32{1'b0}}), .b(subtractor_1_out), .eq(Zero));  // open: gt, lt
  Multiplexer #(.select(2), .width(32), .enable("false")) multiplexer_1 (
    .in0(adder_1_out), .in1(subtractor_1_out), .in2(or_1_out), .out(Y), .sel(ALUOp));  // open: in3
endmodule

module DM (
  input  [31:0] A,
  input  [1:0] LSel,
  input  DMWr,
  input  [1:0] SSel,
  input  Clk,
  input  Rst,
  input  [31:0] WD,
  output [31:0] RD
);

  wire decoder_1_out0, decoder_1_out1, decoder_2_out0, decoder_2_out1, decoder_2_out2, decoder_2_out3;
  wire [7:0] _07_00, _23_16, multiplexer_4_out, multiplexer_5_out, multiplexer_6_out, multiplexer_7_out,
       multiplexer_9_out;
  wire [15:0] multiplexer_8_out;
  wire [15:8] _15_00, _31_16;
  wire [31:0] bit_extender_1_out, bit_extender_2_out, multiplexer_1_out, multiplexer_2_out;

  Multiplexer #(.select(2), .width(32), .enable("false")) multiplexer_1 (
    .in0(WD), .in1(multiplexer_2_out),
    .in2({multiplexer_7_out, multiplexer_6_out, multiplexer_5_out, multiplexer_4_out}),
    .out(multiplexer_1_out), .sel(SSel));  // open: in3
  RAM #(.addrWidth(16), .dataWidth(32), .bus("separate")) ram_1 (
    .addr(A[17:2]), .din(multiplexer_1_out), .data({_31_16, _23_16, _15_00, _07_00}), .str(DMWr), .clk(Clk),
    .clr(Rst));  // open: sel, ld
  Multiplexer #(.width(16), .enable("false")) multiplexer_2 (
    .in0({_15_00, _07_00}), .in1(WD[15:0]), .out(multiplexer_2_out[15:0]), .sel(decoder_1_out0));
  Multiplexer #(.width(16), .enable("false")) multiplexer_3 (
    .in0({_31_16, _23_16}), .in1(WD[15:0]), .out(multiplexer_2_out[31:16]), .sel(decoder_1_out1));
  Multiplexer #(.width(8), .enable("false")) multiplexer_4 (
    .in0(_07_00), .in1(WD[7:0]), .out(multiplexer_4_out), .sel(decoder_2_out0));
  Multiplexer #(.width(8), .enable("false")) multiplexer_5 (
    .in0(_15_00), .in1(WD[7:0]), .out(multiplexer_5_out), .sel(decoder_2_out1));
  Multiplexer #(.width(8), .enable("false")) multiplexer_6 (
    .in0(_23_16), .in1(WD[7:0]), .out(multiplexer_6_out), .sel(decoder_2_out2));
  Multiplexer #(.width(8), .enable("false")) multiplexer_7 (
    .in0(_31_16), .in1(WD[7:0]), .out(multiplexer_7_out), .sel(decoder_2_out3));
  Decoder #(.enable("false")) decoder_1 (.out0(decoder_1_out0), .out1(decoder_1_out1), .sel(A[1]));
  Decoder #(.select(2), .enable("false")) decoder_2 (
    .out0(decoder_2_out0), .out1(decoder_2_out1), .out2(decoder_2_out2), .out3(decoder_2_out3), .sel(A[1:0]));
  assign bit_extender_1_out = {{16{multiplexer_8_out[15]}}, multiplexer_8_out};  // Bit_Extender bit_extender_1
  Multiplexer #(.width(16), .enable("false")) multiplexer_8 (
    .in0({_15_00, _07_00}), .in1({_31_16, _23_16}), .out(multiplexer_8_out), .sel(A[1]));
  Multiplexer #(.select(2), .width(8), .enable("false")) multiplexer_9 (
    .in0(_07_00), .in1(_15_00), .in2(_23_16), .in3(_31_16), .out(multiplexer_9_out), .sel(A[1:0]));
  assign bit_extender_2_out = {{24{multiplexer_9_out[7]}}, multiplexer_9_out};  // Bit_Extender bit_extender_2
  Multiplexer #(.select(2), .width(32), .enable("false")) multiplexer_10 (
    .in0({_31_16, _23_16, _15_00, _07_00}), .in1(bit_extender_1_out), .in2(bit_extender_2_out), .out(RD),
    .sel(LSel));  // open: in3

  // Other names for the same wires on the sheet: _15_00[7:0] = _07_00; _15_08[7:0] = _15_00; _31_16[7:0] = _23_16;
  //   _31_24[7:0] = _31_16; bitjudge[1:0] = A[1:0]; halfjudge = A[1]

  // Notes on the sheet:
  //   lb
  //   lh
endmodule

module PC (
  input  [31:0] DI,
  input  Clk,
  input  Rst,
  output [31:0] DO
);

  Register #(.width(32)) register_1 (.D(DI), .Q(DO), .clk(Clk), .clr(Rst));  // open: en
endmodule

module IM (
  input  [31:0] in_1,
  output [31:0] out_2
);

  ROM #(.addrWidth(16), .dataWidth(32)) rom_1 (.addr(in_1[17:2]), .data(out_2));  // open: sel
endmodule

module register_init (
  input  [31:0] init,
  input  [31:0] D,
  input  en,
  input  clk,
  input  rst,
  output [31:0] Q
);

  wire counter_1_carry;
  wire [31:0] multiplexer_1_out, register_1_q;

  Multiplexer #(.width(32)) multiplexer_1 (.in0(Q), .in1(D), .out(multiplexer_1_out), .sel(en));  // open: en
  Pull_Resistor #(.pull(1)) pull_resistor_1 (.node(en));
  Register #(.width(32)) register_1 (.D(multiplexer_1_out), .Q(register_1_q), .clk(clk), .clr(rst));  // open: en
  Counter #(.width(1), .max('h1), .ongoal("stay")) counter_1 (
    .carry(counter_1_carry), .clk(clk), .clr(rst));  // open: load, D, count, Q
  Pull_Resistor pull_resistor_2 (.node(init));
  Multiplexer #(.width(32)) multiplexer_2 (.in0(init), .in1(register_1_q), .out(Q), .sel(counter_1_carry));  // open: en
endmodule
