// Logisim project 4bit_sort.circ as structural Verilog: 3 circuits, main circuit 1bit_swap
module _1bit_swap (
  input  a,
  input  b,
  input  s,
  output o1,
  output o2
);

  wire and_1_out, and_2_out, and_3_out, and_4_out, not_1_out, not_2_out;

  not not_1 (not_1_out, s);
  not not_2 (not_2_out, s);
  and and_1 (and_1_out, b, s);
  and and_2 (and_2_out, a, not_1_out);
  and and_3 (and_3_out, a, s);
  and and_4 (and_4_out, b, not_2_out);
  or or_1 (o1, and_1_out, and_2_out);
  or or_2 (o2, and_3_out, and_4_out);
endmodule

module _4bit_swap (
  input  [3:0] I1,
  input  [3:0] I2,
  output [3:0] O1,
  output [3:0] O2
);

  wire comparator_1_gt;
  wire [3:0] and_1_out, and_2_out, and_3_out, and_4_out, bit_extender_1_out, not_1_out, not_2_out;

  Comparator #(.width(4), .mode("unsigned")) comparator_1 (.a(I1), .b(I2), .gt(comparator_1_gt));  // open: eq, lt
  assign bit_extender_1_out = {{3{comparator_1_gt}}, comparator_1_gt};  // Bit_Extender bit_extender_1
  assign not_1_out = ~bit_extender_1_out;  // NOT_Gate not_1, 4 bits wide
  assign not_2_out = ~bit_extender_1_out;  // NOT_Gate not_2, 4 bits wide
  assign and_1_out = I2 & bit_extender_1_out;  // AND_Gate and_1, 4 bits wide
  assign and_2_out = I1 & not_1_out;  // AND_Gate and_2, 4 bits wide
  assign and_3_out = I1 & bit_extender_1_out;  // AND_Gate and_3, 4 bits wide
  assign and_4_out = I2 & not_2_out;  // AND_Gate and_4, 4 bits wide
  assign O1 = and_1_out | and_2_out;  // OR_Gate or_1, 4 bits wide
  assign O2 = and_3_out | and_4_out;  // OR_Gate or_2, 4 bits wide
endmodule

module _4bit_sort (
  input  [3:0] A,
  input  [3:0] B,
  input  [3:0] C,
  input  [3:0] D,
  output [3:0] _1,
  output [3:0] _2,
  output [3:0] _3,
  output [3:0] _4
);

  wire [3:0] A1, A2, B1, B2, C1, n4bit_swap_1_o2, n4bit_swap_2_o2, n4bit_swap_4_o2;

  _4bit_swap u_4bit_swap_1 (.I1(A), .I2(B), .O1(A1), .O2(n4bit_swap_1_o2));
  _4bit_swap u_4bit_swap_2 (.I1(A1), .I2(B1), .O1(A2), .O2(n4bit_swap_2_o2));
  _4bit_swap u_4bit_swap_3 (.I1(A2), .I2(B2), .O1(_1), .O2(_2));
  _4bit_swap u_4bit_swap_4 (.I1(C), .I2(n4bit_swap_1_o2), .O1(B1), .O2(n4bit_swap_4_o2));
  _4bit_swap u_4bit_swap_5 (.I1(C1), .I2(n4bit_swap_2_o2), .O1(B2), .O2(_3));
  _4bit_swap u_4bit_swap_6 (.I1(D), .I2(n4bit_swap_4_o2), .O1(C1), .O2(_4));
endmodule
