// Logisim project Fibonacci.circ as structural Verilog: 3 circuits, main circuit main
module main (
  input  [2:0] \input ,
  output [3:0] \output 
);

  wire clk, en;
  wire [3:0] adder_1_out, pre_q;

  cnt cnt_1 (.\input (\input ), .clock(clk), .isreached(en), .rst(1'b0));
  Clock clock_1 (.out(clk));
  Register #(.width(4)) now (.D(pre_q), .en(en), .Q(\output ), .clk(clk), .clr(1'b0));
  register_default_1 pre (.D(adder_1_out), .clk(clk), .Q(pre_q), .en(en), .rst(1'b0));
  // Probe on pre_q
  Adder #(.width(4)) adder_1 (.a(\output ), .b(pre_q), .out(adder_1_out));  // open: cin, cout
  // Probe on adder_1_out

  // Notes on the sheet:
  //   next
endmodule

module cnt (
  input  [2:0] \input ,
  input  clock,
  input  rst,
  output isreached
);

  wire [3:0] bit_extender_1_out, counter_1_q;

  Counter #(.width(4), .max('h7), .ongoal("stay")) counter_1 (
    .Q(counter_1_q), .clk(clock), .clr(rst));  // open: load, D, count, carry
  assign bit_extender_1_out = {{1{1'b0}}, \input };  // Bit_Extender bit_extender_1
  Comparator #(.width(4)) comparator_1 (.a(bit_extender_1_out), .b(counter_1_q), .gt(isreached));  // open: eq, lt
endmodule

module register_default_1 (
  input  [3:0] D,
  input  en,
  input  clk,
  input  rst,
  output [3:0] Q
);

  wire counter_1_carry;
  wire [3:0] register_1_q;

  Register #(.width(4)) register_1 (.D(D), .en(en), .Q(register_1_q), .clk(clk), .clr(rst));
  Counter #(.width(1), .max('h1), .ongoal("stay")) counter_1 (
    .carry(counter_1_carry), .clk(clk), .clr(rst));  // open: load, D, count, Q
  Multiplexer #(.width(4)) multiplexer_1 (
    .in0(4'b0001), .in1(register_1_q), .out(Q), .sel(counter_1_carry));  // open: en
endmodule
