// Logisim project init_reg.circ as structural Verilog: 1 circuit, main circuit main
module main (
  input  [7:0] in_1,
  input  in_2
);

  wire clock_1_out, counter_1_carry;
  wire [7:0] multiplexer_1_out, register_1_q;

  Clock clock_1 (.out(clock_1_out));
  Register register_1 (.D(in_1), .Q(register_1_q), .clk(clock_1_out));  // open: en, clr
  Counter #(.width(1), .max('h1), .ongoal("stay")) counter_1 (
    .carry(counter_1_carry), .clk(clock_1_out), .clr(in_2));  // open: load, D, count, Q
  Multiplexer #(.width(8)) multiplexer_1 (
    .in0(8'h1), .in1(register_1_q), .out(multiplexer_1_out), .sel(counter_1_carry));  // open: en
  // Probe on multiplexer_1_out
endmodule
