// Logisim project mod5-v1.circ as structural Verilog: 2 circuits, main circuit mod5
module mod5 (
  input  In,
  input  reset,
  output _0,
  output _1,
  output _2,
  output _3,
  output _4
);

  wire clock_1_out, not_1_out, not_2_out, S_0_1_4_out, S_2_3_out;
  wire [4:0] set_1_out_3;

  and and_1 (set_1_out_3[2], In, S_0_1_4_out);
  and and_2 (set_1_out_3[3], In, S_2_3_out);
  not not_1 (not_1_out, In);
  and and_3 (set_1_out_3[1], not_1_out, S_0_1_4_out);
  and and_4 (set_1_out_3[4], not_2_out, S_2_3_out);
  not not_2 (not_2_out, In);
  Clock clock_1 (.out(clock_1_out));
  set set_1 (.out_3(set_1_out_3[0]), .in_1(clock_1_out), .in_2(reset));
  Register #(.width(5)) register_1 (
    .D(set_1_out_3), .Q({_4, _3, _2, _1, _0}), .clk(clock_1_out), .clr(reset));  // open: en
  or S_0_1_4 (S_0_1_4_out, _0, _1, _4);
  or S_2_3 (S_2_3_out, _3, _2);
endmodule

module set (
  input  in_1,
  input  in_2,
  output out_3
);

  wire register_1_q;

  nand nand_1 (out_3, 1'b1, register_1_q);
  Register #(.width(1)) register_1 (.D(1'b1), .Q(register_1_q), .clk(in_1), .clr(in_2));  // open: en
endmodule
