// Logisim project mod5-v2.circ as structural Verilog: 1 circuit, main circuit mod5
module mod5 (
  input  In,
  output _0,
  output _1,
  output _2,
  output _3,
  output _4
);

  wire clock_1_out, nor_1_out, not_1_out, not_2_out, S_0_1_4_out, S_2_3_out;
  wire [4:0] register_1_q;
  wire [4:1] and_3_out;

  and and_1 (and_3_out[2], In, S_0_1_4_out);
  and and_2 (and_3_out[3], In, S_2_3_out);
  not not_1 (not_1_out, In);
  and and_3 (and_3_out[1], not_1_out, S_0_1_4_out);
  and and_4 (and_3_out[4], not_2_out, S_2_3_out);
  not not_2 (not_2_out, In);
  Clock clock_1 (.out(clock_1_out));
  Register #(.width(5), .trigger("falling")) register_1 (
    .D({and_3_out, 1'b0}), .Q(register_1_q), .clk(clock_1_out));  // open: en, clr
  Multiplexer #(.width(5)) multiplexer_1 (
    .in0(register_1_q), .in1(5'b00001), .out({_4, _3, _2, _1, _0}), .sel(nor_1_out));  // open: en
  nor nor_1 (nor_1_out, register_1_q[0], register_1_q[1], register_1_q[2], register_1_q[3], register_1_q[4]);
  or S_0_1_4 (S_0_1_4_out, _0, _1, _4);
  or S_2_3 (S_2_3_out, _3, _2);
endmodule
