// Logisim project mod5-v3.circ as structural Verilog: 1 circuit, main circuit mod5
module mod5 (
  input  In,
  output _0,
  output _1,
  output _2,
  output _3,
  output _4
);

  wire clock_1_out, not_2_out, not_3_out;
  wire [0:0] not_1_out;
  wire [1:0] register_1_q;

  not not_1 (not_1_out[0], In);
  Clock clock_1 (.out(clock_1_out));
  not not_2 (not_2_out, register_1_q[1]);
  Register #(.width(2)) register_1 (.D({In, not_1_out[0]}), .Q(register_1_q), .clk(clock_1_out));  // open: en, clr
  and and_1 (_1, not_2_out, not_3_out);
  and and_2 (_3, register_1_q[1], In);
  not not_3 (not_3_out, In);
  and and_3 (_2, not_2_out, In);
  and and_4 (_4, register_1_q[1], not_3_out);

  assign _0 = 1'b0;
endmodule
