// Logisim project swap.circ as structural Verilog: 1 circuit, main circuit swap
module swap (
  input  I1,
  input  I2,
  input  S,
  output out_4,
  output O2
);

  wire and_1_out, xor_1_out;

  xor xor_1 (xor_1_out, I1, I2);
  and and_1 (and_1_out, xor_1_out, S);
  xor xor_2 (out_4, I1, and_1_out);
  xor xor_3 (O2, I2, and_1_out);
endmodule
