// Logisim project thingamajig.circ as structural Verilog: 1 circuit, main circuit main
module main (
  input  in_1,
  output out_2
);

  wire clock_1_out, counter_1_q;
  wire [1:0] multiplexer_1_out, multiplexer_2_out, multiplexer_3_out, multiplexer_4_out, multiplexer_5_out,
       register_1_q;

  Multiplexer #(.width(2)) multiplexer_1 (.in0(2'b10), .in1(2'b11), .out(multiplexer_1_out), .sel(in_1));  // open: en
  Multiplexer #(.width(2)) multiplexer_2 (.in0(2'b10), .in1(2'b11), .out(multiplexer_2_out), .sel(in_1));  // open: en
  Multiplexer #(.width(2)) multiplexer_3 (.in0(2'b10), .in1(2'b11), .out(multiplexer_3_out), .sel(in_1));  // open: en
  // Probe on multiplexer_4_out
  Multiplexer #(.select(2), .width(2)) multiplexer_4 (
    .in1(multiplexer_1_out), .in2(multiplexer_2_out), .in3(multiplexer_3_out), .out(multiplexer_4_out),
    .sel(register_1_q));  // open: in0, en
  Clock clock_1 (.out(clock_1_out));
  Counter #(.width(1), .max('h1), .ongoal("stay")) counter_1 (
    .Q(counter_1_q), .clk(clock_1_out));  // open: load, D, count, carry, clr
  Multiplexer #(.width(2)) multiplexer_5 (
    .in0(2'b01), .in1(multiplexer_4_out), .out(multiplexer_5_out), .sel(counter_1_q));  // open: en
  Multiplexer #(.select(2)) multiplexer_6 (
    .in1(1'b0), .in2(1'b0), .in3(1'b1), .out(out_2), .sel(multiplexer_4_out));  // open: in0, en
  Register #(.width(2)) register_1 (.D(multiplexer_5_out), .Q(register_1_q), .clk(clock_1_out));  // open: en, clr
  // Probe on register_1_q
endmodule
