// Logisim project 也有苦劳.circ as structural Verilog
module h1 (
  input  S2,
  input  S1,
  input  S0,
  output Q2,
  output Q1,
  output Q0
);

  wire and_1_out, and_2_out, and_3_out, not_1_out, not_2_out, not_3_out, not_4_out;

  not not_1 (not_1_out, S2);
  not not_2 (not_2_out, S2);
  not not_3 (not_3_out, S2);
  not not_4 (not_4_out, S0);
  and and_1 (and_1_out, not_1_out, S0);
  and and_2 (and_2_out, not_2_out, S1);
  and and_3 (and_3_out, not_3_out, not_4_out);
  or or_1 (Q2, and_1_out, and_2_out);
  or or_2 (Q1, and_3_out, S1);

  assign Q0 = S0;
endmodule

module leftShift (
  input  S2,
  input  S1,
  input  S0,
  input  D7,
  input  D6,
  input  D5,
  input  D4,
  input  D3,
  input  D2,
  input  D1,
  input  D0,
  output Q7,
  output Q6,
  output Q5,
  output Q4,
  output Q3,
  output Q2,
  output Q1,
  output Q0
);

  wire and_1_out, and_2_out, and_3_out, and_4_out, and_5_out, and_6_out, and_7_out, and_8_out, and_9_out,
       and_10_out, and_11_out, and_12_out, and_13_out, and_14_out, and_15_out, and_16_out, and_17_out,
       and_18_out, and_19_out, and_20_out, and_21_out, and_22_out, and_23_out, and_24_out, and_25_out,
       and_26_out, and_27_out, and_28_out, and_29_out, and_30_out, and_31_out, and_32_out, and_33_out,
       and_34_out, and_35_out, and_36_out, and_37_out, and_38_out, and_39_out, and_40_out, and_41_out,
       and_42_out, and_43_out, and_44_out, and_45_out, and_46_out, and_47_out, and_48_out, and_49_out,
       and_50_out, and_51_out, and_52_out, and_53_out, and_54_out, and_55_out, and_56_out, and_57_out,
       and_58_out, and_59_out, and_60_out, and_61_out, and_62_out, and_63_out, and_64_out, not_1_out,
       not_2_out, not_3_out, not_4_out, not_5_out, not_6_out, not_7_out, not_8_out, not_9_out, not_10_out,
       not_11_out, not_12_out, not_13_out, not_14_out, not_15_out, not_16_out, not_17_out, not_18_out,
       not_19_out, not_20_out, not_21_out, not_22_out, not_23_out, not_24_out, not_25_out, not_26_out,
       not_27_out, not_28_out, not_29_out, not_30_out, not_31_out, not_32_out, not_33_out, not_34_out,
       not_35_out, not_36_out, not_37_out, not_38_out, not_39_out, not_40_out, not_41_out, not_42_out,
       not_43_out, not_44_out, not_45_out, not_46_out, not_47_out, not_48_out, not_49_out, not_50_out,
       not_51_out, not_52_out, not_53_out, not_54_out, not_55_out, not_56_out, not_57_out, not_58_out,
       not_59_out, not_60_out, not_61_out, not_62_out, not_63_out, not_64_out, not_65_out, not_66_out,
       not_67_out, not_68_out, not_69_out, not_70_out, not_71_out, not_72_out, not_73_out, not_74_out,
       not_75_out, not_76_out, not_77_out, not_78_out, not_79_out, not_80_out, not_81_out, not_82_out,
       not_83_out, not_84_out, not_85_out, not_86_out, not_87_out, not_88_out, not_89_out, not_90_out,
       not_91_out, not_92_out, not_93_out, not_94_out, not_95_out, not_96_out;

  not not_1 (not_1_out, S2);
  not not_2 (not_2_out, S1);
  not not_3 (not_3_out, S0);
  not not_4 (not_4_out, S2);
  not not_5 (not_5_out, S1);
  not not_6 (not_6_out, S2);
  not not_7 (not_7_out, S0);
  not not_8 (not_8_out, S2);
  not not_9 (not_9_out, S1);
  not not_10 (not_10_out, S0);
  not not_11 (not_11_out, S1);
  not not_12 (not_12_out, S0);
  not not_13 (not_13_out, S2);
  not not_14 (not_14_out, S1);
  not not_15 (not_15_out, S0);
  not not_16 (not_16_out, S2);
  not not_17 (not_17_out, S1);
  not not_18 (not_18_out, S2);
  not not_19 (not_19_out, S0);
  not not_20 (not_20_out, S2);
  not not_21 (not_21_out, S1);
  not not_22 (not_22_out, S0);
  not not_23 (not_23_out, S1);
  not not_24 (not_24_out, S0);
  not not_25 (not_25_out, S2);
  not not_26 (not_26_out, S1);
  not not_27 (not_27_out, S0);
  not not_28 (not_28_out, S2);
  not not_29 (not_29_out, S1);
  not not_30 (not_30_out, S2);
  not not_31 (not_31_out, S0);
  not not_32 (not_32_out, S2);
  not not_33 (not_33_out, S1);
  not not_34 (not_34_out, S0);
  not not_35 (not_35_out, S1);
  not not_36 (not_36_out, S0);
  not not_37 (not_37_out, S2);
  not not_38 (not_38_out, S1);
  not not_39 (not_39_out, S0);
  not not_40 (not_40_out, S2);
  not not_41 (not_41_out, S1);
  not not_42 (not_42_out, S2);
  not not_43 (not_43_out, S0);
  not not_44 (not_44_out, S2);
  not not_45 (not_45_out, S1);
  not not_46 (not_46_out, S0);
  not not_47 (not_47_out, S1);
  not not_48 (not_48_out, S0);
  not not_49 (not_49_out, S2);
  not not_50 (not_50_out, S1);
  not not_51 (not_51_out, S0);
  not not_52 (not_52_out, S2);
  not not_53 (not_53_out, S1);
  not not_54 (not_54_out, S2);
  not not_55 (not_55_out, S0);
  not not_56 (not_56_out, S2);
  not not_57 (not_57_out, S1);
  not not_58 (not_58_out, S0);
  not not_59 (not_59_out, S1);
  not not_60 (not_60_out, S0);
  not not_61 (not_61_out, S2);
  not not_62 (not_62_out, S1);
  not not_63 (not_63_out, S0);
  not not_64 (not_64_out, S2);
  not not_65 (not_65_out, S1);
  not not_66 (not_66_out, S2);
  not not_67 (not_67_out, S0);
  not not_68 (not_68_out, S2);
  not not_69 (not_69_out, S1);
  not not_70 (not_70_out, S0);
  not not_71 (not_71_out, S1);
  not not_72 (not_72_out, S0);
  not not_73 (not_73_out, S2);
  not not_74 (not_74_out, S1);
  not not_75 (not_75_out, S0);
  not not_76 (not_76_out, S2);
  not not_77 (not_77_out, S1);
  not not_78 (not_78_out, S2);
  not not_79 (not_79_out, S0);
  not not_80 (not_80_out, S2);
  not not_81 (not_81_out, S1);
  not not_82 (not_82_out, S0);
  not not_83 (not_83_out, S1);
  not not_84 (not_84_out, S0);
  not not_85 (not_85_out, S2);
  not not_86 (not_86_out, S1);
  not not_87 (not_87_out, S0);
  not not_88 (not_88_out, S2);
  not not_89 (not_89_out, S1);
  not not_90 (not_90_out, S2);
  not not_91 (not_91_out, S0);
  not not_92 (not_92_out, S2);
  not not_93 (not_93_out, S1);
  not not_94 (not_94_out, S0);
  not not_95 (not_95_out, S1);
  not not_96 (not_96_out, S0);
  and and_1 (and_1_out, not_1_out, not_2_out, not_3_out, D7);
  and and_2 (and_2_out, not_4_out, not_5_out, S0, D6);
  and and_3 (and_3_out, not_6_out, S1, not_7_out, D5);
  and and_4 (and_4_out, not_8_out, S1, S0, D4);
  and and_5 (and_5_out, S2, not_9_out, not_10_out, D3);
  and and_6 (and_6_out, S2, not_11_out, S0, D2);
  and and_7 (and_7_out, S2, S1, not_12_out, D1);
  and and_8 (and_8_out, S2, S1, S0, D0);
  and and_9 (and_9_out, not_13_out, not_14_out, not_15_out, D6);
  and and_10 (and_10_out, not_16_out, not_17_out, S0, D5);
  and and_11 (and_11_out, not_18_out, S1, not_19_out, D4);
  and and_12 (and_12_out, not_20_out, S1, S0, D3);
  and and_13 (and_13_out, S2, not_21_out, not_22_out, D2);
  and and_14 (and_14_out, S2, not_23_out, S0, D1);
  and and_15 (and_15_out, S2, S1, not_24_out, D0);
  and and_16 (and_16_out, S2, S1, S0, D7);
  and and_17 (and_17_out, not_25_out, not_26_out, not_27_out, D5);
  and and_18 (and_18_out, not_28_out, not_29_out, S0, D4);
  and and_19 (and_19_out, not_30_out, S1, not_31_out, D3);
  and and_20 (and_20_out, not_32_out, S1, S0, D2);
  and and_21 (and_21_out, S2, not_33_out, not_34_out, D1);
  and and_22 (and_22_out, S2, not_35_out, S0, D0);
  and and_23 (and_23_out, S2, S1, not_36_out, D7);
  and and_24 (and_24_out, S2, S1, S0, D6);
  and and_25 (and_25_out, not_37_out, not_38_out, not_39_out, D4);
  and and_26 (and_26_out, not_40_out, not_41_out, S0, D3);
  and and_27 (and_27_out, not_42_out, S1, not_43_out, D2);
  and and_28 (and_28_out, not_44_out, S1, S0, D1);
  and and_29 (and_29_out, S2, not_45_out, not_46_out, D0);
  and and_30 (and_30_out, S2, not_47_out, S0, D7);
  and and_31 (and_31_out, S2, S1, not_48_out, D6);
  and and_32 (and_32_out, S2, S1, S0, D5);
  and and_33 (and_33_out, not_49_out, not_50_out, not_51_out, D3);
  and and_34 (and_34_out, not_52_out, not_53_out, S0, D2);
  and and_35 (and_35_out, not_54_out, S1, not_55_out, D1);
  and and_36 (and_36_out, not_56_out, S1, S0, D0);
  and and_37 (and_37_out, S2, not_57_out, not_58_out, D7);
  and and_38 (and_38_out, S2, not_59_out, S0, D6);
  and and_39 (and_39_out, S2, S1, not_60_out, D5);
  and and_40 (and_40_out, S2, S1, S0, D4);
  and and_41 (and_41_out, not_61_out, not_62_out, not_63_out, D2);
  and and_42 (and_42_out, not_64_out, not_65_out, S0, D1);
  and and_43 (and_43_out, not_66_out, S1, not_67_out, D0);
  and and_44 (and_44_out, not_68_out, S1, S0, D7);
  and and_45 (and_45_out, S2, not_69_out, not_70_out, D6);
  and and_46 (and_46_out, S2, not_71_out, S0, D5);
  and and_47 (and_47_out, S2, S1, not_72_out, D4);
  and and_48 (and_48_out, S2, S1, S0, D3);
  and and_49 (and_49_out, not_73_out, not_74_out, not_75_out, D1);
  and and_50 (and_50_out, not_76_out, not_77_out, S0, D0);
  and and_51 (and_51_out, not_78_out, S1, not_79_out, D7);
  and and_52 (and_52_out, not_80_out, S1, S0, D6);
  and and_53 (and_53_out, S2, not_81_out, not_82_out, D5);
  and and_54 (and_54_out, S2, not_83_out, S0, D4);
  and and_55 (and_55_out, S2, S1, not_84_out, D3);
  and and_56 (and_56_out, S2, S1, S0, D2);
  and and_57 (and_57_out, not_85_out, not_86_out, not_87_out, D0);
  and and_58 (and_58_out, not_88_out, not_89_out, S0, D7);
  and and_59 (and_59_out, not_90_out, S1, not_91_out, D6);
  and and_60 (and_60_out, not_92_out, S1, S0, D5);
  and and_61 (and_61_out, S2, not_93_out, not_94_out, D4);
  and and_62 (and_62_out, S2, not_95_out, S0, D3);
  and and_63 (and_63_out, S2, S1, not_96_out, D2);
  and and_64 (and_64_out, S2, S1, S0, D1);
  or or_1 (Q7, and_1_out, and_2_out, and_3_out, and_4_out, and_5_out, and_6_out, and_7_out, and_8_out);
  or or_2 (Q6, and_9_out, and_10_out, and_11_out, and_12_out, and_13_out, and_14_out, and_15_out, and_16_out);
  or or_3 (Q5, and_17_out, and_18_out, and_19_out, and_20_out, and_21_out, and_22_out, and_23_out, and_24_out);
  or or_4 (Q4, and_25_out, and_26_out, and_27_out, and_28_out, and_29_out, and_30_out, and_31_out, and_32_out);
  or or_5 (Q3, and_33_out, and_34_out, and_35_out, and_36_out, and_37_out, and_38_out, and_39_out, and_40_out);
  or or_6 (Q2, and_41_out, and_42_out, and_43_out, and_44_out, and_45_out, and_46_out, and_47_out, and_48_out);
  or or_7 (Q1, and_49_out, and_50_out, and_51_out, and_52_out, and_53_out, and_54_out, and_55_out, and_56_out);
  or or_8 (Q0, and_57_out, and_58_out, and_59_out, and_60_out, and_61_out, and_62_out, and_63_out, and_64_out);
endmodule
