// Logisim project register_init.circ as structural Verilog: 1 circuit, main circuit register_init
module register_init (
  input  [31:0] in_1
);

  wire [31:0] register_1_q;

  Register #(.width(32)) register_1 (.Q(register_1_q));  // open: D, en, clk, clr
  Multiplexer #(.width(32)) multiplexer_1 (.in0(in_1), .in1(register_1_q));  // open: out, sel, en
endmodule
